# Fritzing sketch smart-collect-iot (saved by Fritzing 0.9.3b)

parts:
  hc-sr1 = hc-sr04
  M1 = AJ-SR04M Module [part_number=AJ-SR04M]
  M2 = AJ-SR04M Module [part_number=AJ-SR04M]
  CPU1 = NodeMCU WROOM ESP 32
  OLED_I2C1 = OLED 128x64 I2C Monochrome Display

nets:
  VCC: hc-sr1.VCC, M1.VCC, M2.VCC, CPU1.pin_17, OLED_I2C1.VDD
  N1: hc-sr1.Trig, CPU1.pin_19
  N2: hc-sr1.Echo, CPU1.pin_21
  GND: hc-sr1.GND, M1.GND, M2.GND, CPU1.pin_18, OLED_I2C1.GND
  N3: M1.Echo, CPU1.pin_23
  N4: M1.Trig, CPU1.pin_22
  N5: M2.Echo, CPU1.pin_24
  N6: M2.Trig, CPU1.pin_25
  N7: CPU1.pin_27, OLED_I2C1.SDA
  N8: CPU1.pin_30, OLED_I2C1.SCK

custom parts:
  AJ-SR04M Module: AJ-SR04M Ultrasonic Distance Measuring Sensor Controller Module, 3-5V DC.
  NodeMCU WROOM ESP 32: 30 pol Development Kit
